# Fritzing sketch TamAIgotchi (saved by Fritzing 1.0.6)
breadboards: 1

parts:
  A1 = Wemos S2 Mini [part_number="WeMos D1 Mini Lite"]
  OLED_I2C1 = OLED 128x64 I2C Monochrome Display
  S1 = Pushbutton [package="[THT]"]
  LED1 = smd LED [color="Red (633nm)" package="0603 [SMD]"]
  Part1 = INMP441
  R1 = Resistor [tolerance=±5% resistance=220 package="1206 [SMD]"]

nets:
  N1: A1.Pin_1, A1.Pin_9
  N2: A1.Pin_2, A1.Pin_10, S1.Pin_3, S1.Pin_4
  N3: A1.Pin_3, A1.Pin_11, Part1.SD
  N4: A1.Pin_4, A1.Pin_12
  N5: A1.Pin_5, A1.Pin_13
  N6: A1.Pin_6, A1.Pin_14
  N7: A1.Pin_7, A1.Pin_15, R1.Pin_1
  VDD: A1.Pin_8, A1.Pin_16, OLED_I2C1.VDD, Part1.VDD
  N8: A1.Pin_17, A1.Pin_25
  GND: A1.Pin_18, A1.Pin_26, OLED_I2C1.GND, S1.Pin_1, S1.Pin_2, LED1.cathode, Part1.GND
  N9: A1.Pin_19, A1.Pin_27, Part1.SCK
  N10: A1.Pin_20, A1.Pin_28, Part1.WS
  N11: A1.Pin_21, A1.Pin_29, OLED_I2C1.SCK
  N12: A1.Pin_22, A1.Pin_30, OLED_I2C1.SDA
  N13: A1.Pin_23, A1.Pin_31
  N14: A1.Pin_24, A1.Pin_32
  N15: LED1.anode, R1.Pin_0

custom parts:
  Wemos S2 Mini: A mini wifi board based on the ESP32-S2FN4R2.
  INMP441: This is a simple breakout board for the INMP441 I2S MEMS microphone.
